# Fritzing sketch AP - Antipanico (saved by Fritzing 0.9.3b)
circuit board: 10cm x 6cm
stripboards: 1

parts:
  Teensy_3_5 = Teensy 3.1
  S1 = SWITCH-MOMENTARY-2 [package=tactile-switch-1101ne]
  J15 = Camdenboss CTB0158-2 [part_number=CTB0158-2 package=THT]
  J18 = screw terminal, 3 pins
  J19 = Camdenboss CTB0158-2 [part_number=CTB0158-2 package=THT]
  R2 = Resistor [tolerance=±5% resistance=10k package=THT]
  KY-1 = Keyes Relay [package=THT]
  C2 = Electrolytic Capacitor [capacitance=0.22mF package="100 mil [THT, electrolytic]"]
  R3 = Resistor [tolerance=±5% resistance=10 package=THT]
  R4 = Resistor [tolerance=±5% resistance=1k package=THT]
  C3 = Ceramic Capacitor [capacitance=100nF package="100 mil [THT, multilayer]"]
  C4 = Ceramic Capacitor [capacitance=10nF package="100 mil [THT, multilayer]"]
  R1 = Resistor [tolerance=±5% resistance=10k package=THT]
  C1 = Ceramic Capacitor [capacitance=10nF package="100 mil [THT, multilayer]"]
  D2 = Schottky Diode [part_number="SR104 RO" package="300 mil [THT]"]
  D1 = Zener Diode [part_number=1N4732A breakdown_voltage=3.6V package="Melf DO-213 AB [SMD]"]

nets (from the breadboard view):
  N1: Teensy_3_5.GND, C2.+, C3.1
  N2: Teensy_3_5.A2/D16, R4.Pin_1, R1.Pin_1, C1.1, D1.cathode
  N3: Teensy_3_5.3V3, S1.1, J15.pin2, J19.pin1
  N4: Teensy_3_5.AGND, J18.pin2, R2.Pin_1, KY-1.ground, C4.0, R1.Pin_0, C1.0, D2.anode, D1.anode
  N5: Teensy_3_5.Vin, J18.pin1, KY-1.power, C2.-, C3.0
  N6: S1.2, J19.pin2, R3.Pin_0
  N7: J15.pin1, R2.Pin_0, C4.1
  N8: J18.pin3, KY-1.signal
  N9: R3.Pin_1, R4.Pin_0, D2.cathode

notes:
  USB 5V
  segnale chiusura porta

custom parts:
  Keyes Relay: The Keyes 5V relay module is suitable for SCM development, home appliance control. It uses a 5V~12V TIL control signal which can control DC / AC signal.
