# Fritzing sketch H - Help (saved by Fritzing 0.9.3b)
stripboards: 1

parts:
  J21 = Camdenboss CTB0158-2 [part_number=CTB0158-2 package=THT]
  R6 = Resistor [tolerance=±5% resistance=10k package=THT]
  R7 = Resistor [tolerance=±5% resistance=1k package=THT]
  R8 = Resistor [tolerance=±5% resistance=10 package=THT]
  Teensy_3_6 = Teensy 3.1
  S2 = SWITCH-MOMENTARY-2 [package=tactile-switch-1101ne]
  C4 = Ceramic Capacitor [capacitance=10nF package="100 mil [THT, multilayer]"]
  C5 = Ceramic Capacitor [capacitance=100nF package="100 mil [THT, multilayer]"]
  C6 = Electrolytic Capacitor [capacitance=0.22mF package="100 mil [THT, electrolytic]"]
  D3 = Zener Diode [part_number=1N4732A breakdown_voltage=3.6V package="Melf DO-213 AB [SMD]"]
  D4 = Schottky Diode [part_number="SR104 RO" package="300 mil [THT]"]

nets:
  N1: J21.pin1, Teensy_3_6.3V3, S2.1
  N2: J21.pin2, R8.Pin_0, S2.2
  N3: R6.Pin_0, Teensy_3_6.AGND, C4.0, D3.anode, D4.anode
  N4: R6.Pin_1, R7.Pin_1, C4.1, D3.cathode
  N5: R7.Pin_0, R8.Pin_1, D4.cathode
  N6: Teensy_3_6.Vin, C5.0, C6.+
  N7: C5.1, C6.-

notes:
  USB 5V
