# Fritzing sketch G10 - Bambole (saved by Fritzing 0.9.3b)
stripboards: 2

parts:
  R59 = Resistor [tolerance=±5% resistance=1k package=THT]
  D4 = Rectifier Diode [part_number=1N4001 package="300 mil [THT]"]
  Q5 = Basic FET N-Channel [package="TO220 [THT]"]
  J32 = screw terminal, 3 pins
  U2 = Luxeon LED [package=luxeon]
  Teensy_3_1 = Teensy 3.1  # not connected
  Componente2 = Adafruit MPR121
  J34 = Screw terminal - 2 pins [package=THT]  # not connected
  J35 = Screw terminal - 2 pins [package=THT]
  J26 = screw terminal, 8 pins
  J36 = Screw terminal - 2 pins [package=THT]  # not connected

nets:
  N1: R59.Pin_0, Q5.gate
  N2: R59.Pin_1, J32.pin3, J26.pin1
  N3: D4.cathode, Q5.drain, J32.pin1, U2.C
  VIN: D4.anode, Q5.source, J32.pin2, U2.A, Componente2.VIN, Componente2.GND
  N4: Componente2.SDA, J35.pin1, J26.pin8
  N5: Componente2.SCL, J35.pin2, J26.pin7

notes:
  Stagnola
  x8

custom parts:
  Adafruit MPR121: Add lots of touch sensors to your next microcontroller project with this easy-to-use 12-channel capacitive touch sensor breakout board, starring the MPR121. This chip can handle up to 12 individual touch pads. The MPR121 has support for only I2C, which can be implemented with nearly any microcontroller. You can select one of 4 addresses with the ADDR pin, for a total of 48 capacitive touch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
