# Fritzing sketch G13 - Cyclette (saved by Fritzing 0.9.3b)
stripboards: 1

parts:
  J8 = Screw terminal - 2 pins [package=THT]
  J9 = Screw terminal - 2 pins [package=THT]
  S3 = Reed switch [package=THT]
  S4 = Reed switch [package=THT]
  S5 = Reed switch [package=THT]
  S6 = Reed switch [package=THT]
  S7 = Reed switch [package=THT]
  S8 = Reed switch [package=THT]
  J10 = Screw terminal - 2 pins [package=THT]
  J11 = Screw terminal - 2 pins [package=THT]
  R1 = Resistor [tolerance=±5% resistance=10k package=THT]
  R2 = Resistor [tolerance=±5% resistance=10k package=THT]
  R3 = Resistor [tolerance=±5% resistance=10k package=THT]
  R4 = Resistor [tolerance=±5% resistance=10k package=THT]
  R5 = Resistor [tolerance=±5% resistance=10k package=THT]
  R6 = Resistor [tolerance=±5% resistance=10k package=THT]
  Teensy_3_1 = Teensy 3.1  # not connected

nets:
  N1: J8.pin1, S6.pin_2, R3.Pin_1
  N2: J8.pin2, S5.pin_2, R4.Pin_1
  N3: J9.pin1, S4.pin_2, R5.Pin_1
  N4: J9.pin2, S3.pin_2, R6.Pin_1
  N5: S3.pin_1, S4.pin_1, S5.pin_1, S6.pin_1, S7.pin_1, S8.pin_1, J11.pin1
  N6: S7.pin_2, J10.pin2, R2.Pin_1
  N7: S8.pin_2, J10.pin1, R1.Pin_1
  N8: J11.pin2, R1.Pin_0, R2.Pin_0, R3.Pin_0, R4.Pin_0, R5.Pin_0, R6.Pin_0

notes:
  USB 5V
  come per i pulsanti
