# Fritzing sketch G4 - Twister (saved by Fritzing 0.9.3b)
stripboards: 1

parts:
  KY-2 = Keyes Relay [package=THT]
  KY-3 = Keyes Relay [package=THT]
  Componente3 = Adafruit MPR121
  J37 = Screw terminal - 2 pins [package=THT]
  J38 = Screw terminal - 2 pins [package=THT]
  J39 = Screw terminal - 2 pins [package=THT]
  Teensy_3_2 = Teensy 3.1
  Componente4 = Adafruit MPR121
  J40 = Screw terminal - 2 pins [package=THT]
  J36 = Screw terminal - 2 pins [package=THT]

nets:
  N1: KY-2.signal, Teensy_3_2.A9/D23, J40.pin2
  N2: KY-2.power, KY-3.power, J38.pin2
  N3: KY-2.ground, KY-3.ground, J36.pin1
  N4: KY-2.C, KY-3.C
  N5: KY-3.signal, Teensy_3_2.A8/D22, J40.pin1
  VIN: Componente3.VIN, Teensy_3_2.Vin, Componente4.VIN
  GND: Componente3.GND, Teensy_3_2.GND, Componente4.GND
  N6: Componente3.SDA, J39.pin1, Teensy_3_2.A4/D18, Componente4.SDA
  N7: Componente3.SCL, J39.pin2, Teensy_3_2.A5/D19, Componente4.SCL
  N8: J37.pin1, Teensy_3_2.A0/D14
  N9: J37.pin2, Teensy_3_2.A1/D15
  N10: Componente4.3.3V, Componente4.ADDR

notes:
  Stagnola
  elettrocalamita
  quadro + diodo + snubber
  12V
  elettrocalamita
  Botola + diodo + snubber
  USB 5V

custom parts:
  Keyes Relay: The Keyes 5V relay module is suitable for SCM development, home appliance control. It uses a 5V~12V TIL control signal which can control DC / AC signal.
  Adafruit MPR121: Add lots of touch sensors to your next microcontroller project with this easy-to-use 12-channel capacitive touch sensor breakout board, starring the MPR121. This chip can handle up to 12 individual touch pads. The MPR121 has support for only I2C, which can be implemented with nearly any microcontroller. You can select one of 4 addresses with the ADDR pin, for a total of 48 capacitive touch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
