# Fritzing sketch G7 - Portafrutta (saved by Fritzing 0.9.3b)
stripboards: 1

parts:
  J13 = screw terminal, 3 pins
  J8 = screw terminal, 3 pins
  Componente3 = HX711 Weighing Sensor Module
  Componente1 = HX711 Weighing Sensor Module
  Componente2 = HX711 Weighing Sensor Module
  Componente4 = Arduino Uno (Rev3)
  J9 = screw terminal, 3 pins
  J14 = screw terminal, 3 pins

nets:
  GND: J13.pin1, J13.pin2, J13.pin3, Componente3.GND, Componente1.GND, Componente2.GND, Componente4.GND
  VCC: J8.pin1, J8.pin2, J8.pin3, Componente3.VCC, Componente1.VCC, Componente2.VCC, Componente4.5V
  N1: Componente3.DO/RX, Componente4.D2, J9.pin3
  N2: Componente3.CK/TX, Componente1.CK/TX, Componente2.CK/TX, Componente4.D3_PWM, J14.pin1, J14.pin2, J14.pin3
  N3: Componente1.DO/RX, Componente4.D5_PWM, J9.pin1
  N4: Componente2.DO/RX, Componente4.D4, J9.pin2

notes:
  Load Cell
  Teensy
