# Fritzing sketch G1 - Consolle (saved by Fritzing 0.9.3b)
stripboards: 1

parts:
  S9 = Round Pushbutton
  S10 = Round Pushbutton
  S11 = Round Pushbutton
  S12 = Round Pushbutton
  KY-1 = Keyes Relay [package=THT]
  Water_Level_Sensor1 = Water Level Sensor
  D2F1 = D2F-FL Omron Snap Action Limit Switch with Level
  R1 = Resistor [tolerance=±5% resistance=10k package=THT]
  KY-2 = Keyes Relay [package=THT]
  D2F2 = D2F-FL Omron Snap Action Limit Switch with Level
  KY-3 = Keyes Relay [package=THT]
  Teensy_3_1 = Teensy 3.1
  J2 = screw terminal, 5 pins
  J3 = screw terminal, 5 pins
  J5 = screw terminal, 5 pins
  J4 = screw terminal, 8 pins
  R2 = Resistor [tolerance=±5% resistance=10k package=THT]
  R3 = Resistor [tolerance=±5% resistance=10k package=THT]
  J6 = Basic Servo

nets:
  N1: S9.leg0, S10.leg0, S11.leg0, S12.leg0, D2F1.COM, D2F2.COM, Teensy_3_1.AGND, J4.pin3, J4.pin4, J4.pin5, J6.pulse
  N2: S9.leg1, S10.leg1, S11.leg1, S12.leg1, R1.Pin_1, Teensy_3_1.A6/D20
  N3: KY-1.signal, Teensy_3_1.D2, J5.pin3
  VCC: KY-1.power, Water_Level_Sensor1.VCC, KY-2.power, KY-3.power, Teensy_3_1.Vin, J2.pin1, J2.pin2, J2.pin3, J2.pin4, J2.pin5, J4.pin6, J6.vcc
  GND: KY-1.ground, Water_Level_Sensor1.GND, KY-2.ground, KY-3.ground, Teensy_3_1.GND, J3.pin1, J3.pin2, J3.pin3, J3.pin4, J3.pin5, J6.gnd
  N4: Water_Level_Sensor1.SIG, Teensy_3_1.A7/D21, J4.pin1
  N5: D2F1.NO, Teensy_3_1.A5/D19, R2.Pin_1
  N6: R1.Pin_0, Teensy_3_1.3V3, R2.Pin_0, R3.Pin_0
  N7: KY-2.signal, Teensy_3_1.D1, J5.pin2
  N8: D2F2.NO, Teensy_3_1.A4/D18, R3.Pin_1
  N9: KY-3.signal, Teensy_3_1.D0, J5.pin1
  N10: Teensy_3_1.D3, J5.pin4
  N11: Teensy_3_1.D4, J5.pin5
  N12: Teensy_3_1.A8/D22, J4.pin2

notes:
  macchina fumo
  (collegare su CTL)
  orologio
  sportello ingranaggi
  (collegare su CLT)
  fiaccola
  Ingranaggio
  motore ingranaggi
  - Pulsanti tutti pullup completi di diodi
  - Servo ok
  - Acqua collegato con cavo schermato
  - Fumo eventualmente relay 15A
  - sportello elettropistoni
  - motore mosfet con pulldown 10k

custom parts:
  Keyes Relay: The Keyes 5V relay module is suitable for SCM development, home appliance control. It uses a 5V~12V TIL control signal which can control DC / AC signal.
  Water Level Sensor: A water level sensor. This sensor operates at 3V to 5V. The Sig (signal) pin outputs an analogue signal that is in proportion to the amount of water in contact with the sensor.
  D2F-FL Omron Snap Action Limit Switch with Level: Snap action switch with stainless steel lever.
