# Fritzing sketch G14 - Uccelli (saved by Fritzing 0.9.3b)
stripboards: 1

parts:
  Teensy_3_3 = Teensy 3.1  # not connected
  D2F7 = D2F-FL Omron Snap Action Limit Switch with Level
  D2F8 = D2F-FL Omron Snap Action Limit Switch with Level
  J10 = Screw terminal - 2 pins [package=THT]
  J11 = screw terminal, 3 pins
  J12 = Screw terminal - 2 pins [package=THT]
  R8 = Resistor [tolerance=±5% resistance=10k package=THT]
  R9 = Resistor [tolerance=±5% resistance=10k package=THT]
  KY-2 = Keyes Relay [package=THT]
  J9 = screw terminal, 3 pins
  D2F9 = D2F-FL Omron Snap Action Limit Switch with Level
  R10 = Resistor [tolerance=±5% resistance=10k package=THT]

nets:
  N1: D2F7.COM, D2F8.COM, J11.pin1, J11.pin2, J11.pin3, KY-2.ground, D2F9.COM
  N2: D2F7.NO, R8.Pin_1, J9.pin2
  N3: D2F8.NO, R9.Pin_1, J9.pin1, D2F9.NO
  N4: J10.pin1, KY-2.signal
  N5: J12.pin1, J12.pin2, KY-2.power
  N6: R8.Pin_0, R9.Pin_0, R10.Pin_0

notes:
  USB 5V
  12V
  elettrocalamita + diodo + snubber

custom parts:
  D2F-FL Omron Snap Action Limit Switch with Level: Snap action switch with stainless steel lever.
  Keyes Relay: The Keyes 5V relay module is suitable for SCM development, home appliance control. It uses a 5V~12V TIL control signal which can control DC / AC signal.
