# Fritzing sketch G2 - Tastiera (saved by Fritzing 0.9.3b)
stripboards: 1

parts:
  R2 = Resistor [tolerance=±5% resistance=4.7k package=THT]
  Teensy_LC = Teensy 3.1
  D2F1 = D2F-FL Omron Snap Action Limit Switch with Level
  D2F2 = D2F-FL Omron Snap Action Limit Switch with Level
  D2F3 = D2F-FL Omron Snap Action Limit Switch with Level
  D2F4 = D2F-FL Omron Snap Action Limit Switch with Level
  R3 = Resistor [tolerance=±5% resistance=4.7k package=THT]
  C7 = Ceramic Capacitor [capacitance=100nF package="100 mil [THT, multilayer]"]
  C8 = Electrolytic Capacitor [capacitance=1µF package="100 mil [THT, electrolytic]"]
  J1 = Screw terminal - 2 pins [package=THT]
  J2 = Screw terminal - 2 pins [package=THT]
  J3 = Screw terminal - 2 pins [package=THT]

nets:
  N1: R2.Pin_0, Teensy_LC.3V3, R3.Pin_0
  N2: R2.Pin_1, Teensy_LC.A5/D19, J2.pin2
  N3: Teensy_LC.GND, D2F1.COM, D2F2.COM, D2F3.COM, D2F4.COM, C7.0, C8.-, J3.pin2
  N4: Teensy_LC.A4/D18, R3.Pin_1, J2.pin1
  N5: Teensy_LC.Vin, C7.1, C8.+, J1.pin2

notes:
  PCF8574
  (x3)
  USB 5V
  x 24

custom parts:
  D2F-FL Omron Snap Action Limit Switch with Level: Snap action switch with stainless steel lever.
