# Fritzing sketch G4 - Roccia (saved by Fritzing 0.9.3b)
stripboards: 1

parts:
  KY-1 = Keyes Relay [package=THT]
  Teensy_3_1 = Teensy 3.1  # not connected
  D2F4 = D2F-FL Omron Snap Action Limit Switch with Level
  R5 = Resistor [tolerance=±5% resistance=10k package=THT]
  J1 = screw terminal, 4 pins
  J3 = Screw terminal - 2 pins [package=THT]  # not connected
  J4 = screw terminal, 3 pins
  J2 = Screw terminal - 2 pins [package=THT]

nets:
  N1: KY-1.signal, J2.pin1, J2.pin2
  N2: KY-1.power, J1.pin4
  N3: KY-1.ground, D2F4.COM, J4.pin1, J4.pin2, J4.pin3
  N4: D2F4.NO, R5.Pin_1
  N5: R5.Pin_0, J1.pin2

notes:
  12V
  USB 5V
  elettrocalam tonda 20kg + diodo + snubber

custom parts:
  Keyes Relay: The Keyes 5V relay module is suitable for SCM development, home appliance control. It uses a 5V~12V TIL control signal which can control DC / AC signal.
  D2F-FL Omron Snap Action Limit Switch with Level: Snap action switch with stainless steel lever.
