# Fritzing sketch G6 - Totem (saved by Fritzing 0.9.3b)
stripboards: 1

parts:
  Teensy_3_2 = Teensy 3.1  # not connected
  HC-SR04_Sensor_1 = HC-SR04 Ultrasonic Distance Sensor
  HC-SR04_Sensor_2 = HC-SR04 Ultrasonic Distance Sensor
  J11 = screw terminal, 8 pins

nets:
  VCC: HC-SR04_Sensor_1.VCC, HC-SR04_Sensor_2.VCC, J11.pin8
  N1: HC-SR04_Sensor_1.TRIG, J11.pin5
  N2: HC-SR04_Sensor_1.ECHO, J11.pin3
  GND: HC-SR04_Sensor_1.GND, HC-SR04_Sensor_2.GND, J11.pin7
  N3: HC-SR04_Sensor_2.TRIG, J11.pin4
  N4: HC-SR04_Sensor_2.ECHO, J11.pin2

notes:
  USB 5V
  sequenza luci + elettrovalvola
